# Fritzing sketch carrinho (saved by Fritzing 0.9.3b)
# 18650 Li-ion Battery: CC-BY Dr Kristofer Chan, King's College London/Remote-research.org

parts:
  Carrinho = Arduino Nano (Rev3.0)
  Sensor_ultrasônico_hc-sr04 = hc-sr04
  Reg_Tensao_7805 = Voltage Regulator - 5V [package="TO220 [THT]"]
  BMS_3S = 3S-BMS
  BAT1 = 18650 Li-ion Battery [package=battery-18650]
  BAT2 = 18650 Li-ion Battery [package=battery-18650]
  BAT3 = 18650 Li-ion Battery [package=battery-18650]
  M2 = Getriebemotor
  M3 = Getriebemotor
  Sensor_de_Linha_BFD-1000 = 5-ir-array-sensor [package=THT]
  Driver_L293D = L293D [package=THT]
  C1 = Electrolytic Capacitor [capacitance=1µF package="300 mil [THT, electrolytic]"]
  C2 = Electrolytic Capacitor [capacitance=1µF package="300 mil [THT, electrolytic]"]

nets:
  N1: Carrinho.D2, Carrinho.D3, Carrinho.D4, Carrinho.D5, Driver_L293D.In_1, Driver_L293D.In_2, Driver_L293D.In_3, Driver_L293D.In_4
  N2: Carrinho.D6, Carrinho.D7, Driver_L293D.Enable_1, Driver_L293D.Enable_2
  N3: Carrinho.D8, Sensor_ultrasônico_hc-sr04.Trig
  N4: Carrinho.D9, Sensor_ultrasônico_hc-sr04.Echo
  N5: Carrinho.D10, Sensor_de_Linha_BFD-1000.CLP, Sensor_de_Linha_BFD-1000.S4
  N6: Carrinho.VIN, Reg_Tensao_7805.output_voltage, Driver_L293D.+V, C1.-, C2.-
  GND: Carrinho.GND, Sensor_ultrasônico_hc-sr04.GND, Sensor_de_Linha_BFD-1000.GND, Driver_L293D.0V
  VCC: Carrinho.5V, Sensor_ultrasônico_hc-sr04.VCC, Sensor_de_Linha_BFD-1000.VCC, Driver_L293D.+Vmotor
  N7: Carrinho.A5, Sensor_de_Linha_BFD-1000.Near, Sensor_de_Linha_BFD-1000.S2
  N8: Carrinho.A4, Sensor_de_Linha_BFD-1000.S5
  N9: Carrinho.A2, Sensor_de_Linha_BFD-1000.S3
  N10: Carrinho.A0, Sensor_de_Linha_BFD-1000.S1
  N11: Reg_Tensao_7805.input_voltage, BMS_3S.+
  N12: Reg_Tensao_7805.GND, BMS_3S.-, C1.+, C2.+
  N13: BMS_3S.0V, BAT1.+
  N14: BMS_3S.4.2V, BAT1.-, BAT2.-, BAT3.+
  N15: BMS_3S.8.4V, BAT3.-
  N16: BMS_3S.12.6V, BAT2.+
  N17: M2.pin_1, Driver_L293D.Out_2_(_Controlled_by_Enable_1_)
  N18: M2.pin_2, Driver_L293D.Out_1_(_Controlled_by_Enable_1_)
  N19: M3.pin_1, Driver_L293D.Out_4_(_Controlled_by_Enable_2_)
  N20: M3.pin_2, Driver_L293D.Out_3_(_Controlled_by_Enable_2_)

notes:
  | 1 |motores| 2 |

custom parts:
  3S-BMS: 3S-BMS LIPO battery charger / protection unit. Note pcb does not match the board as it will likely connect with wires, so pcb is 6 pads suitable for .1in header pins.
  18650 Li-ion Battery: 18650 li-ion Battery Standard 18650 battery with interactive connectors Creative Common Attribution 4.0 International (CC-BY 4.0) license. Any use of this part requires attribution of Dr Kristofer Chan, Department of Geography, King's College London. Contact kristofer.chan [at] kcl.ac.uk OR kris [at] remote-research.org for further information.
  5-ir-array-sensor: 5 IR array sensor.

// code stored in the sketch: carrinho.ino
const int ENA = 11;
const int IN1 = 12;
const int IN2 = 10;
const int ENB = 6;
const int IN3 = 7;
const int IN4 = 5;

void setup() {
  pinMode(ENA, OUTPUT);
  pinMode(IN1, OUTPUT);
  pinMode(IN2, OUTPUT);
  pinMode(ENB, OUTPUT);
  pinMode(IN3, OUTPUT);
  pinMode(IN4, OUTPUT);

  Serial.begin(9600);
  Serial.println("Iniciando motores para frente!");

  digitalWrite(IN1, HIGH);
  digitalWrite(IN2, LOW);

  digitalWrite(IN3, HIGH);
  digitalWrite(IN4, LOW);

  analogWrite(ENA, 255);
  analogWrite(ENB, 255);
}

void loop() {
}
