# Fritzing sketch sensor bfd 5000 (saved by Fritzing 0.9.3b)

parts:
  Componente1 = Arduino Nano (Rev3.0)
  M1 = 5-ir-array-sensor [package=THT]

nets:
  GND: Componente1.GND, M1.GND
  N1: Componente1.D2, M1.S1
  N2: Componente1.D3, M1.S2
  N3: Componente1.D4, M1.S3
  N4: Componente1.D5, M1.S4
  N5: Componente1.D6, M1.S5
  N6: Componente1.D7, M1.CLP
  N7: Componente1.D8, M1.Near
  5V: Componente1.5V, M1.VCC

custom parts:
  5-ir-array-sensor: 5 IR array sensor.
